# Fritzing sketch sketch (saved by Fritzing 0.9.3b)
breadboards: 1

parts:
  WeMos_D1_Mini1 = WeMos D1 Mini
  Tx1 = mystery part, 3 pins [chip_label=?]
  Rx1 = mystery part, 4 pins [chip_label=?]

nets:
  N1: WeMos_D1_Mini1.5V, Tx1.pin2, Tx1.pin3, Rx1.pin2, Rx1.pin3
  N2: WeMos_D1_Mini1.D2, Rx1.pin1
  N3: WeMos_D1_Mini1.D3, Tx1.pin1

notes:
  Transmitter
  receiver
